// Logisim project alu.circ as structural Verilog: 1 circuit, main circuit alu
module alu (
  input  [31:0] A,
  input  [31:0] B,
  input  [3:0] ALUSel,
  output [31:0] ALUResult
);

  wire comparator_1_gt;
  wire [4:0] bit_extender_1_out, bit_extender_2_out, bit_extender_3_out;
  wire [31:0] add0, and7, bsel15, mul8, mulh9, mulhu11, or6, sll1, slt2, sra13, srl5, sub12, xor4;

  Bit_Extender #(.in_width(32), .out_width(5), .\type ("zero")) bit_extender_1 (.in(B), .out(bit_extender_1_out));
  Bit_Extender #(.in_width(32), .out_width(5), .\type ("zero")) bit_extender_2 (.in(B), .out(bit_extender_2_out));
  Bit_Extender #(.in_width(32), .out_width(5), .\type ("zero")) bit_extender_3 (.in(B), .out(bit_extender_3_out));
  Adder #(.width(32)) adder_1 (.a(A), .b(B), .out(add0));  // open: cin, cout
  Shifter #(.width(32)) shifter_1 (.in(A), .\dist (bit_extender_1_out), .out(sll1));
  Comparator #(.mode("unsigned"), .width(32)) comparator_1 (.a(A), .b(B), .gt(comparator_1_gt));  // open: eq, lt
  assign xor4 = A ^ B;  // XOR_Gate xor_1, 32 bits wide
  Shifter #(.shift("lr"), .width(32)) shifter_2 (.in(A), .\dist (bit_extender_2_out), .out(srl5));
  assign and7 = A & B;  // AND_Gate and_1, 32 bits wide
  assign or6 = A | B;  // OR_Gate or_1, 32 bits wide
  Multiplier #(.mode("twosComplement"), .width(32)) multiplier_1 (.a(A), .b(B), .out(mul8));  // open: cin, cout
  Multiplier #(.mode("twosComplement"), .width(32)) multiplier_2 (.a(A), .b(B), .cout(mulh9));  // open: out, cin
  Multiplier #(.width(32)) multiplier_3 (.a(A), .b(B), .cout(mulhu11));  // open: out, cin
  Subtractor #(.width(32)) subtractor_1 (.a(A), .b(B), .out(sub12));  // open: bin, bout
  Shifter #(.shift("ar"), .width(32)) shifter_3 (.in(A), .\dist (bit_extender_3_out), .out(sra13));
  Multiplexer #(.width(32)) multiplexer_1 (.in0(A), .in1(B), .out(bsel15), .sel(1'b1));
  assign slt2 = {{31{1'b0}}, comparator_1_gt};  // Bit_Extender bit_extender_4
  Multiplexer #(.select(4), .width(32)) multiplexer_2 (
    .in0(add0), .in1(sll1), .in2(slt2), .in4(xor4), .in5(srl5), .in6(or6), .in7(and7), .in8(mul8),
    .in9(mulh9), .in11(mulhu11), .in12(sub12), .in13(sra13), .in15(bsel15), .out(ALUResult), .sel(ALUSel));  // open: in3, in10, in14

  // Notes on the sheet:
  //   INPUTS to your circuit
  //   DON'T CHANGE THE LOCATIONS OF THE INPUTS AND OUTPUTS!
  //   OUTPUT from your circuit
endmodule
