// Logisim project imm-gen.circ as structural Verilog: 1 circuit, main circuit imm_gen
module imm_gen (
  input  [31:0] Instruction,
  input  [2:0] ImmSel,
  output [31:0] Immediate
);

  wire [30:12] Btype;
  wire [31:0] shifter_1_out;
  wire [31:11] Stype;
  wire [31:20] Jtype;

  assign Btype = {{18{Instruction[31]}}, Instruction[31]};  // Bit_Extender bit_extender_1
  assign Jtype = {{11{Instruction[31]}}, Instruction[31]};  // Bit_Extender bit_extender_2
  assign Stype = {{20{Instruction[31]}}, Instruction[31]};  // Bit_Extender bit_extender_3
  Shifter #(.shift("ar"), .width(32)) shifter_1 (.in(Instruction), .\dist (5'b10100), .out(shifter_1_out));
  Multiplexer #(.select(3), .width(32)) multiplexer_1 (
    .in0(shifter_1_out), .in1({Stype, Instruction[30:25], Instruction[11:7]}),
    .in2({Instruction[31], Btype, Instruction[7], Instruction[30:25], Instruction[11:8], 1'b0}),
    .in3({Instruction[31:12], {12{1'b0}}}),
    .in4({Jtype, Instruction[19:12], Instruction[20], Instruction[30:21], 1'b0}), .out(Immediate),
    .sel(ImmSel));  // open: in5, in6, in7

  // Other names for the same wires on the sheet: Jtype[19:1] = {Instruction[19:12], Instruction[20], Instruction[30:21]};
  //   Utype[31:12] = Instruction[31:12];
  //   Btype (some bits) = {Instruction[31], Instruction[7], Instruction[30:25], Instruction[11:8]};
  //   Stype[10:0] = {Instruction[30:25], Instruction[11:7]}

  // Notes on the sheet:
  //   INPUTS to your circuit
  //   DON'T CHANGE THE LOCATIONS OF THE INPUTS AND OUTPUTS!
  //   OUTPUT from your circuit
endmodule
