// Logisim project partial-store.circ as structural Verilog: 1 circuit, main circuit partial_store
module partial_store (
  input  [31:0] Instruction,
  input  [31:0] MemAddress,
  input  [31:0] DataFromReg,
  input  MemWEn,
  output [3:0] MemWriteMask,
  output [31:0] DataToMem
);

  wire [1:0] bit_extender_1_out;
  wire [3:0] multiplexer_4_out, sbmask, shmask;
  wire [31:0] sb, sh, shifter_1_out, shifter_2_out, shifter_3_out, shifter_4_out;

  Shifter #(.width(32)) shifter_1 (.in({{24{1'b0}}, DataFromReg[7:0]}), .\dist (5'b01000), .out(shifter_1_out));
  Shifter #(.width(32)) shifter_2 (.in({{24{1'b0}}, DataFromReg[7:0]}), .\dist (5'b10000), .out(shifter_2_out));
  Shifter #(.width(32)) shifter_3 (.in({{24{1'b0}}, DataFromReg[7:0]}), .\dist (5'b11000), .out(shifter_3_out));
  Shifter #(.width(32)) shifter_4 (.in({{16{1'b0}}, DataFromReg[15:0]}), .\dist (5'b10000), .out(shifter_4_out));
  Multiplexer #(.select(2), .width(32)) multiplexer_1 (
    .in0({{24{1'b0}}, DataFromReg[7:0]}), .in1(shifter_1_out), .in2(shifter_2_out), .in3(shifter_3_out),
    .out(sb), .sel(MemAddress[1:0]));
  Multiplexer #(.width(32)) multiplexer_2 (
    .in0({{16{1'b0}}, DataFromReg[15:0]}), .in1(shifter_4_out), .out(sh), .sel(MemAddress[1]));
  Multiplexer #(.select(2), .width(32)) multiplexer_3 (
    .in0(sb), .in1(sh), .in2(DataFromReg), .out(DataToMem), .sel(Instruction[13:12]));  // open: in3
  assign bit_extender_1_out = {{1{MemWEn}}, MemWEn};  // Bit_Extender bit_extender_1
  Multiplexer #(.width(4)) multiplexer_4 (.in0(4'b0000), .in1(4'b1111), .out(multiplexer_4_out), .sel(MemWEn));
  Shifter #(.width(4)) shifter_5 (.in({3'b000, MemWEn}), .\dist (MemAddress[1:0]), .out(sbmask));
  Shifter #(.width(4)) shifter_6 (.in({2'b00, bit_extender_1_out}), .\dist ({MemAddress[1], 1'b0}), .out(shmask));
  Multiplexer #(.select(2), .width(4)) multiplexer_5 (
    .in0(sbmask), .in1(shmask), .in2(multiplexer_4_out), .out(MemWriteMask), .sel(Instruction[13:12]));  // open: in3

  // Notes on the sheet:
  //   INPUTS to your circuit
  //   DON'T CHANGE THE LOCATIONS OF THE INPUTS AND OUTPUTS!
  //   OUTPUT from your circuit
endmodule
