// Logisim project regfile.circ as structural Verilog: 1 circuit, main circuit regfile
module regfile (
  input  [4:0] ReadIndex1,
  input  [4:0] ReadIndex2,
  input  [4:0] WriteIndex,
  input  [31:0] WriteData,
  input  RegWEn,
  input  clk,
  output [31:0] ra,
  output [31:0] sp,
  output [31:0] t0,
  output [31:0] t1,
  output [31:0] t2,
  output [31:0] s0,
  output [31:0] s1,
  output [31:0] a0,
  output [31:0] ReadData1,
  output [31:0] ReadData2
);

  wire x0A, x0B, x0C, x0D, x0E, x0F, x01, x1A, x1B, x1C, x1D, x1E, x1F, x02, x03, x04, x05, x06, x07, x08,
       x09, x10, x11, x12, x13, x14, x15, x16, x17, x18, x19;
  wire [31:0] a1, a2, a3, a4, a5, a6, a7, gp, s2, s3, s4, s5, s6, s7, s8, s9, s10, s11, t3, t4, t5, t6, tp,
       Zero;

  Demultiplexer #(.select(5)) demultiplexer_1 (
    .out1(x01), .out2(x02), .out3(x03), .out4(x04), .out5(x05), .out6(x06), .out7(x07), .out8(x08),
    .out9(x09), .out10(x0A), .out11(x0B), .out12(x0C), .out13(x0D), .out14(x0E), .out15(x0F), .out16(x10),
    .out17(x11), .out18(x12), .out19(x13), .out20(x14), .out21(x15), .out22(x16), .out23(x17), .out24(x18),
    .out25(x19), .out26(x1A), .out27(x1B), .out28(x1C), .out29(x1D), .out30(x1E), .out31(x1F), .in(RegWEn),
    .sel(WriteIndex));  // open: out0
  assign Zero = {{24{1'b0}}, {8{1'b0}}};  // Bit_Extender bit_extender_1
  Register #(.width(32)) register_1 (.D(WriteData), .en(x01), .clk(clk), .Q(ra));  // open: clr
  Register #(.width(32)) register_2 (.D(WriteData), .en(x02), .clk(clk), .Q(sp));  // open: clr
  Register #(.width(32)) register_3 (.D(WriteData), .en(x03), .clk(clk), .Q(gp));  // open: clr
  Register #(.width(32)) register_4 (.D(WriteData), .en(x04), .clk(clk), .Q(tp));  // open: clr
  Register #(.width(32)) register_5 (.D(WriteData), .en(x05), .clk(clk), .Q(t0));  // open: clr
  Register #(.width(32)) register_6 (.D(WriteData), .en(x06), .clk(clk), .Q(t1));  // open: clr
  Register #(.width(32)) register_7 (.D(WriteData), .en(x07), .clk(clk), .Q(t2));  // open: clr
  Register #(.width(32)) register_8 (.D(WriteData), .en(x08), .clk(clk), .Q(s0));  // open: clr
  Register #(.width(32)) register_9 (.D(WriteData), .en(x09), .clk(clk), .Q(s1));  // open: clr
  Register #(.width(32)) register_10 (.D(WriteData), .en(x0A), .clk(clk), .Q(a0));  // open: clr
  Register #(.width(32)) register_11 (.D(WriteData), .en(x0B), .clk(clk), .Q(a1));  // open: clr
  Register #(.width(32)) register_12 (.D(WriteData), .en(x0C), .clk(clk), .Q(a2));  // open: clr
  Register #(.width(32)) register_13 (.D(WriteData), .en(x0D), .clk(clk), .Q(a3));  // open: clr
  Register #(.width(32)) register_14 (.D(WriteData), .en(x0E), .clk(clk), .Q(a4));  // open: clr
  Register #(.width(32)) register_15 (.D(WriteData), .en(x0F), .clk(clk), .Q(a5));  // open: clr
  Register #(.width(32)) register_16 (.D(WriteData), .en(x10), .clk(clk), .Q(a6));  // open: clr
  Register #(.width(32)) register_17 (.D(WriteData), .en(x11), .clk(clk), .Q(a7));  // open: clr
  Register #(.width(32)) register_18 (.D(WriteData), .en(x12), .clk(clk), .Q(s2));  // open: clr
  Register #(.width(32)) register_19 (.D(WriteData), .en(x13), .clk(clk), .Q(s3));  // open: clr
  Register #(.width(32)) register_20 (.D(WriteData), .en(x14), .clk(clk), .Q(s4));  // open: clr
  Register #(.width(32)) register_21 (.D(WriteData), .en(x15), .clk(clk), .Q(s5));  // open: clr
  Register #(.width(32)) register_22 (.D(WriteData), .en(x16), .clk(clk), .Q(s6));  // open: clr
  Register #(.width(32)) register_23 (.D(WriteData), .en(x17), .clk(clk), .Q(s7));  // open: clr
  Register #(.width(32)) register_24 (.D(WriteData), .en(x18), .clk(clk), .Q(s8));  // open: clr
  Register #(.width(32)) register_25 (.D(WriteData), .en(x19), .clk(clk), .Q(s9));  // open: clr
  Register #(.width(32)) register_26 (.D(WriteData), .en(x1A), .clk(clk), .Q(s10));  // open: clr
  Register #(.width(32)) register_27 (.D(WriteData), .en(x1B), .clk(clk), .Q(s11));  // open: clr
  Register #(.width(32)) register_28 (.D(WriteData), .en(x1C), .clk(clk), .Q(t3));  // open: clr
  Register #(.width(32)) register_29 (.D(WriteData), .en(x1D), .clk(clk), .Q(t4));  // open: clr
  Register #(.width(32)) register_30 (.D(WriteData), .en(x1E), .clk(clk), .Q(t5));  // open: clr
  Register #(.width(32)) register_31 (.D(WriteData), .en(x1F), .clk(clk), .Q(t6));  // open: clr
  Multiplexer #(.select(5), .width(32)) multiplexer_1 (
    .in0(Zero), .in1(ra), .in2(sp), .in3(gp), .in4(tp), .in5(t0), .in6(t1), .in7(t2), .in8(s0), .in9(s1),
    .in10(a0), .in11(a1), .in12(a2), .in13(a3), .in14(a4), .in15(a5), .in16(a6), .in17(a7), .in18(s2),
    .in19(s3), .in20(s4), .in21(s5), .in22(s6), .in23(s7), .in24(s8), .in25(s9), .in26(s10), .in27(s11),
    .in28(t3), .in29(t4), .in30(t5), .in31(t6), .out(ReadData1), .sel(ReadIndex1));
  Multiplexer #(.select(5), .width(32)) multiplexer_2 (
    .in0(Zero), .in1(ra), .in2(sp), .in3(gp), .in4(tp), .in5(t0), .in6(t1), .in7(t2), .in8(s0), .in9(s1),
    .in10(a0), .in11(a1), .in12(a2), .in13(a3), .in14(a4), .in15(a5), .in16(a6), .in17(a7), .in18(s2),
    .in19(s3), .in20(s4), .in21(s5), .in22(s6), .in23(s7), .in24(s8), .in25(s9), .in26(s10), .in27(s11),
    .in28(t3), .in29(t4), .in30(t5), .in31(t6), .out(ReadData2), .sel(ReadIndex2));

  // Notes on the sheet:
  //   INPUTS to your circuit
  //   DON'T CHANGE THE LOCATIONS OF THE INPUTS AND OUTPUTS!
  //   These are DEBUG/TEST outputs from your circuit.
  //   OUTPUTS from your circuit
endmodule
